// Logisim project CPU.circ as structural Verilog: 2 circuits, main circuit main
module main (
);

  wire alu_1_f_out, ALU_INPUT_SWAP, and_1_out, and_2_out, and_4_out, and_5_out, and_6_out, and_7_out, ASLEEP,
       B2I, BOOTSTRAPPING, CLK, CLK_RAW, comparator_1_eq, comparator_2_eq, comparator_3_eq, comparator_4_eq,
       controlled_buffer_3_out, controlled_buffer_12_out, controlled_buffer_13_out, controlled_buffer_25_out,
       controlled_buffer_26_out, DO_JUMP, FAULT, FAULTED, FLAG_BUS, FLAG_REG_A, FLAG_REG_B, HALT, HALTED,
       I2B, INSN_END, INTERNAL_FLAG_REG_A, INTERNAL_FLAG_REG_B, JMP, JMP_IF, JMP_IFN, LOAD_A, LOAD_ALU,
       LOAD_ALU_FLAG, LOAD_B, LOAD_FLAG_A, LOAD_FLAG_B, LOAD_INTERNAL_A, LOAD_INTERNAL_B,
       LOAD_INTERNAL_FLAG_A, LOAD_INTERNAL_FLAG_B, LOAD_PROG, LOAD_RAM, not_1_out, not_2_out, not_4_out,
       not_5_out, not_6_out, not_7_out, not_8_out, not_9_out, or_1_out, or_3_out, or_4_out, PROG_NEXT,
       pull_resistor_1_node, pull_resistor_3_node, pull_resistor_4_node, PWR, RESET, SLEEP, STORE_A,
       STORE_ALU_OP, STORE_B, STORE_DISPLAY, STORE_FLAG_A, STORE_FLAG_B, STORE_INSN, STORE_INTERNAL_A,
       STORE_INTERNAL_B, STORE_INTERNAL_FLAG_A, STORE_INTERNAL_FLAG_B, STORE_RAM, STORE_RAM_ADDR, SWAP_FLAGS,
       SWAP_INT, SWAP_INTERNAL_FLAGS, SWAP_INTERNAL_INT, ZERO_FAULT, ZERO_FAULTED;
  wire [1:0] pull_resistor_9_node;
  wire [5:0] bitselector_1_out;
  wire [7:0] pull_resistor_2_node, STEP;
  wire [15:0] alu_1_out, bit_extender_1_out, BUS, controlled_buffer_6_out, controlled_buffer_7_out,
       controlled_buffer_8_out, controlled_buffer_9_out, counter_3_q, DISPLAY, INSN, INTERNAL_REG_A,
       INTERNAL_REG_B, PROG_ADDR, pull_resistor_5_node, pull_resistor_14_node, REG_A, REG_B, register_1_q,
       register_2_q, register_8_q, rom_1_data;
  wire [31:0] pull_resistor_15_node, pull_resistor_25_node;
  wire [31:8] rom_3_data;

  LED led_1 (.in(PWR));
  D_Flip_Flop #(.trigger("falling")) d_ff_1 (.D(HALT), .clk(CLK), .Q(HALTED), .reset(RESET));  // open: Qn, preset
  D_Flip_Flop #(.trigger("falling")) d_ff_2 (.D(FAULT), .clk(CLK), .Q(FAULTED), .reset(RESET));  // open: Qn, preset
  D_Flip_Flop #(.trigger("falling")) d_ff_3 (
    .D(ZERO_FAULT), .clk(CLK), .Q(ZERO_FAULTED), .reset(RESET));  // open: Qn, preset
  ROM #(.addrWidth(16), .dataWidth(16)) rom_1 (.addr(PROG_ADDR), .data(rom_1_data));
  Pull_Resistor #(.pull(1)) pull_resistor_1 (.node(pull_resistor_1_node));
  Pull_Resistor pull_resistor_2 (.node(pull_resistor_2_node));
  Clock clock_1 (.out(CLK_RAW));
  Button button_1 (.out(RESET));
  // Probe on DISPLAY
  Counter #(.width(16), .max('hffff)) counter_1 (
    .clr(RESET), .load(DO_JUMP), .up(pull_resistor_3_node), .count(PROG_NEXT), .clk(CLK), .D(BUS),
    .Q(PROG_ADDR));  // open: carry
  Pull_Resistor #(.pull(1)) pull_resistor_3 (.node(pull_resistor_3_node));
  Register #(.width(16)) register_1 (.D(BUS), .en(STORE_INSN), .clk(CLK), .Q(register_1_q), .clr(RESET));
  Counter counter_2 (
    .clr(RESET), .load(INSN_END), .up(pull_resistor_1_node), .count(pull_resistor_1_node), .clk(CLK),
    .D(pull_resistor_2_node), .Q(STEP));  // open: carry
  Counter #(.width(16), .max('hffff)) counter_3 (
    .clr(RESET), .load(SLEEP), .up(pull_resistor_4_node), .count(ASLEEP), .clk(CLK_RAW), .D(BUS),
    .Q(counter_3_q));  // open: carry
  Pull_Resistor pull_resistor_4 (.node(pull_resistor_4_node));
  // Probe on DISPLAY
  // Probe on BUS
  // Probe on FLAG_BUS
  and and_1 (and_1_out, JMP_IF, FLAG_BUS);
  or or_1 (or_1_out, and_1_out, and_2_out);
  and and_2 (and_2_out, ~FLAG_BUS, JMP_IFN);  // AND_Gate
  D_Flip_Flop d_ff_4 (.D(1'b1), .clk(CLK), .Qn(BOOTSTRAPPING), .reset(RESET));  // open: Q, preset
  // Probe on DISPLAY
  LED led_2 (.in(FAULTED));
  LED led_3 (.in(ZERO_FAULTED));
  or or_2 (DO_JUMP, JMP, or_1_out);
  not not_1 (not_1_out, BOOTSTRAPPING);
  assign INSN = not_1_out ? register_1_q : 16'bz;  // Controlled_Buffer controlled_buffer_1
  assign INSN = BOOTSTRAPPING ? {16{1'b1}} : 16'bz;  // Controlled_Buffer controlled_buffer_2
  Pull_Resistor pull_resistor_5 (.node(pull_resistor_5_node));
  not not_2 (not_2_out, ASLEEP);
  assign controlled_buffer_3_out = PWR ? CLK_RAW : 1'bz;  // Controlled_Buffer controlled_buffer_3
  assign CLK = not_2_out ? controlled_buffer_3_out : 1'bz;  // Controlled_Buffer controlled_buffer_4
  Pull_Resistor pull_resistor_6 (.node(LOAD_PROG));
  assign BUS = LOAD_PROG ? rom_1_data : 16'bz;  // Controlled_Buffer controlled_buffer_5
  Comparator #(.width(16)) comparator_1 (
    .a(counter_3_q), .b(pull_resistor_5_node), .eq(comparator_1_eq));  // open: gt, lt
  not not_3 (ASLEEP, comparator_1_eq);
  Pull_Resistor pull_resistor_7 (.node(CLK));
  nor nor_1 (PWR, HALTED, ZERO_FAULTED, FAULTED);
  assign controlled_buffer_6_out = not_4_out ? BUS : 16'bz;  // Controlled_Buffer controlled_buffer_6
  not not_4 (not_4_out, SWAP_INT);
  not not_5 (not_5_out, SWAP_INT);
  assign controlled_buffer_7_out = not_5_out ? BUS : 16'bz;  // Controlled_Buffer controlled_buffer_7
  assign controlled_buffer_8_out = ALU_INPUT_SWAP ? REG_A : 16'bz;  // Controlled_Buffer controlled_buffer_8
  assign controlled_buffer_9_out = not_6_out ? REG_A : 16'bz;  // Controlled_Buffer controlled_buffer_9
  assign controlled_buffer_8_out = not_6_out ? REG_B : 16'bz;  // Controlled_Buffer controlled_buffer_10
  assign controlled_buffer_9_out = ALU_INPUT_SWAP ? REG_B : 16'bz;  // Controlled_Buffer controlled_buffer_11
  not not_6 (not_6_out, ALU_INPUT_SWAP);
  Pull_Resistor pull_resistor_8 (.node(ALU_INPUT_SWAP));
  assign controlled_buffer_12_out = ALU_INPUT_SWAP ? FLAG_REG_A : 1'bz;  // Controlled_Buffer controlled_buffer_12
  not not_7 (not_7_out, ALU_INPUT_SWAP);
  assign controlled_buffer_13_out = not_7_out ? FLAG_REG_A : 1'bz;  // Controlled_Buffer controlled_buffer_13
  assign controlled_buffer_12_out = not_7_out ? FLAG_REG_B : 1'bz;  // Controlled_Buffer controlled_buffer_14
  assign controlled_buffer_13_out = ALU_INPUT_SWAP ? FLAG_REG_B : 1'bz;  // Controlled_Buffer controlled_buffer_15
  ROM #(.addrWidth(24), .dataWidth(32)) rom_2 (
    .addr({INSN, STEP}),
    .data({B2I, I2B, STORE_DISPLAY, STORE_ALU_OP, STORE_INTERNAL_FLAG_B, STORE_INTERNAL_FLAG_A, STORE_FLAG_B, STORE_FLAG_A, STORE_INTERNAL_B, STORE_INTERNAL_A, STORE_B, STORE_A, LOAD_ALU_FLAG, LOAD_ALU, LOAD_INTERNAL_FLAG_B, LOAD_INTERNAL_FLAG_A, LOAD_FLAG_B, LOAD_FLAG_A, LOAD_INTERNAL_B, LOAD_INTERNAL_A, LOAD_B, LOAD_A, JMP_IFN, JMP_IF, JMP, STORE_INSN, LOAD_PROG, PROG_NEXT, INSN_END, SLEEP, FAULT, HALT}));
  or or_3 (or_3_out, SWAP_INT, STORE_A);
  or or_4 (or_4_out, SWAP_INT, STORE_B);
  Register #(.width(16)) register_2 (.D(BUS), .en(STORE_ALU_OP), .clk(CLK), .Q(register_2_q), .clr(RESET));
  LED led_4 (.in(CLK));
  Register #(.width(16)) register_3 (.D(controlled_buffer_6_out), .en(or_3_out), .clk(CLK), .Q(REG_A), .clr(RESET));
  assign controlled_buffer_7_out = SWAP_INT ? REG_A : 16'bz;  // Controlled_Buffer controlled_buffer_16
  assign controlled_buffer_6_out = SWAP_INT ? REG_B : 16'bz;  // Controlled_Buffer controlled_buffer_17
  Register #(.width(16)) register_4 (.D(controlled_buffer_7_out), .en(or_4_out), .clk(CLK), .Q(REG_B), .clr(RESET));
  Register #(.width(16)) register_5 (.D(BUS), .en(STORE_INTERNAL_A), .clk(CLK), .Q(INTERNAL_REG_A), .clr(RESET));
  Register #(.width(16)) register_6 (.D(BUS), .en(STORE_INTERNAL_B), .clk(CLK), .Q(INTERNAL_REG_B), .clr(RESET));
  BitSelector #(.width(16), .group(6)) bitselector_1 (
    .in(register_2_q), .out(bitselector_1_out), .sel(pull_resistor_9_node));
  Pull_Resistor pull_resistor_9 (.node(pull_resistor_9_node));
  assign BUS = LOAD_A ? REG_A : 16'bz;  // Controlled_Buffer controlled_buffer_18
  Pull_Resistor pull_resistor_10 (.node(LOAD_A));
  assign BUS = LOAD_B ? REG_B : 16'bz;  // Controlled_Buffer controlled_buffer_19
  Pull_Resistor pull_resistor_11 (.node(LOAD_B));
  assign BUS = LOAD_INTERNAL_A ? INTERNAL_REG_A : 16'bz;  // Controlled_Buffer controlled_buffer_20
  Pull_Resistor pull_resistor_12 (.node(LOAD_INTERNAL_A));
  assign BUS = LOAD_INTERNAL_B ? INTERNAL_REG_B : 16'bz;  // Controlled_Buffer controlled_buffer_21
  Pull_Resistor pull_resistor_13 (.node(LOAD_INTERNAL_B));
  ALU alu_1 (
    .OP(bitselector_1_out), .A(controlled_buffer_9_out), .B(controlled_buffer_8_out), .OUT(alu_1_out),
    .F_OUT(alu_1_f_out), .FLAG_A(controlled_buffer_13_out), .FLAG_B(controlled_buffer_12_out));
  Comparator #(.width(16), .mode("unsigned")) comparator_2 (
    .a(BUS), .b(pull_resistor_14_node), .eq(comparator_2_eq));  // open: gt, lt
  Pull_Resistor pull_resistor_14 (.node(pull_resistor_14_node));
  Pull_Resistor pull_resistor_15 (.node(pull_resistor_15_node));
  Pull_Resistor pull_resistor_16 (.node({B2I, I2B, STORE_DISPLAY, STORE_ALU_OP, STORE_INTERNAL_FLAG_B, STORE_INTERNAL_FLAG_A, STORE_FLAG_B, STORE_FLAG_A, STORE_INTERNAL_B, STORE_INTERNAL_A, STORE_B, STORE_A, LOAD_ALU_FLAG, LOAD_ALU, LOAD_INTERNAL_FLAG_B, LOAD_INTERNAL_FLAG_A, LOAD_FLAG_B, LOAD_FLAG_A, LOAD_INTERNAL_B, LOAD_INTERNAL_A, LOAD_B, LOAD_A, JMP_IFN, JMP_IF, JMP, STORE_INSN, LOAD_PROG, PROG_NEXT, INSN_END, SLEEP, FAULT, HALT}));
  LED led_5 (.in(CLK));
  Pull_Resistor pull_resistor_17 (.node(LOAD_ALU));
  Pull_Resistor pull_resistor_18 (.node(LOAD_ALU_FLAG));
  Pull_Resistor pull_resistor_19 (.node(I2B));
  assign FLAG_BUS = I2B ? ~comparator_2_eq : 1'bz;  // Controlled_Inverter controlled_inverter_1
  Pull_Resistor pull_resistor_20 (.node(B2I));
  assign bit_extender_1_out = {{15{FLAG_BUS}}, FLAG_BUS};  // Bit_Extender bit_extender_1
  assign BUS = B2I ? bit_extender_1_out : 16'bz;  // Controlled_Buffer controlled_buffer_22
  Comparator #(.width(32), .mode("unsigned")) comparator_3 (
    .a(pull_resistor_15_node),
    .b({B2I, I2B, STORE_DISPLAY, STORE_ALU_OP, STORE_INTERNAL_FLAG_B, STORE_INTERNAL_FLAG_A, STORE_FLAG_B, STORE_FLAG_A, STORE_INTERNAL_B, STORE_INTERNAL_A, STORE_B, STORE_A, LOAD_ALU_FLAG, LOAD_ALU, LOAD_INTERNAL_FLAG_B, LOAD_INTERNAL_FLAG_A, LOAD_FLAG_B, LOAD_FLAG_A, LOAD_INTERNAL_B, LOAD_INTERNAL_A, LOAD_B, LOAD_A, JMP_IFN, JMP_IF, JMP, STORE_INSN, LOAD_PROG, PROG_NEXT, INSN_END, SLEEP, FAULT, HALT}),
    .eq(comparator_3_eq));  // open: gt, lt
  assign BUS = LOAD_ALU ? alu_1_out : 16'bz;  // Controlled_Buffer controlled_buffer_23
  assign FLAG_BUS = LOAD_ALU_FLAG ? alu_1_f_out : 1'bz;  // Controlled_Buffer controlled_buffer_24
  Register #(.width(16)) register_7 (.D(BUS), .en(STORE_DISPLAY), .clk(CLK), .Q(DISPLAY), .clr(RESET));
  Register #(.width(16)) register_8 (.D(BUS), .en(STORE_RAM_ADDR), .clk(CLK), .Q(register_8_q), .clr(RESET));
  RAM #(.addrWidth(16), .dataWidth(16)) ram_1 (
    .addr(register_8_q), .we(STORE_RAM), .oe(LOAD_RAM), .clk(CLK), .data(BUS));
  and and_3 (ZERO_FAULT, comparator_3_eq, comparator_4_eq);
  and and_4 (and_4_out, CLK, STORE_FLAG_A);
  ROM #(.addrWidth(24), .dataWidth(32)) rom_3 (
    .addr({INSN, STEP}),
    .data({rom_3_data, LOAD_RAM, STORE_RAM, STORE_RAM_ADDR, ALU_INPUT_SWAP, SWAP_INTERNAL_FLAGS, SWAP_INTERNAL_INT, SWAP_FLAGS, SWAP_INT}));
  assign controlled_buffer_25_out = not_8_out ? FLAG_BUS : 1'bz;  // Controlled_Buffer controlled_buffer_25
  not not_8 (not_8_out, SWAP_FLAGS);
  not not_9 (not_9_out, SWAP_FLAGS);
  assign controlled_buffer_26_out = not_9_out ? FLAG_BUS : 1'bz;  // Controlled_Buffer controlled_buffer_26
  and and_5 (and_5_out, CLK, STORE_FLAG_B);
  D_Flip_Flop d_ff_5 (
    .D(controlled_buffer_25_out), .clk(and_4_out), .Q(FLAG_REG_A), .reset(RESET));  // open: Qn, preset
  assign controlled_buffer_25_out = SWAP_FLAGS ? FLAG_REG_A : 1'bz;  // Controlled_Buffer controlled_buffer_27
  assign controlled_buffer_26_out = SWAP_FLAGS ? FLAG_REG_B : 1'bz;  // Controlled_Buffer controlled_buffer_28
  D_Flip_Flop d_ff_6 (
    .D(controlled_buffer_26_out), .clk(and_5_out), .Q(FLAG_REG_B), .reset(RESET));  // open: Qn, preset
  D_Flip_Flop d_ff_7 (.D(FLAG_BUS), .clk(and_6_out), .Q(INTERNAL_FLAG_REG_A), .reset(RESET));  // open: Qn, preset
  and and_6 (and_6_out, CLK, STORE_INTERNAL_FLAG_A);
  D_Flip_Flop d_ff_8 (.D(FLAG_BUS), .clk(and_7_out), .Q(INTERNAL_FLAG_REG_B), .reset(RESET));  // open: Qn, preset
  and and_7 (and_7_out, CLK, STORE_INTERNAL_FLAG_B);
  assign FLAG_BUS = LOAD_FLAG_A ? FLAG_REG_A : 1'bz;  // Controlled_Buffer controlled_buffer_29
  Pull_Resistor pull_resistor_21 (.node(LOAD_FLAG_A));
  assign FLAG_BUS = LOAD_FLAG_B ? FLAG_REG_B : 1'bz;  // Controlled_Buffer controlled_buffer_30
  Pull_Resistor pull_resistor_22 (.node(LOAD_FLAG_B));
  assign FLAG_BUS = LOAD_INTERNAL_FLAG_A ? INTERNAL_FLAG_REG_A : 1'bz;  // Controlled_Buffer controlled_buffer_31
  Pull_Resistor pull_resistor_23 (.node(LOAD_INTERNAL_FLAG_A));
  assign FLAG_BUS = LOAD_INTERNAL_FLAG_B ? INTERNAL_FLAG_REG_B : 1'bz;  // Controlled_Buffer controlled_buffer_32
  Pull_Resistor pull_resistor_24 (.node(LOAD_INTERNAL_FLAG_B));
  Pull_Resistor pull_resistor_25 (.node(pull_resistor_25_node));
  Pull_Resistor pull_resistor_26 (.node({rom_3_data, LOAD_RAM, STORE_RAM, STORE_RAM_ADDR, ALU_INPUT_SWAP, SWAP_INTERNAL_FLAGS, SWAP_INTERNAL_INT, SWAP_FLAGS, SWAP_INT}));
  Comparator #(.width(32), .mode("unsigned")) comparator_4 (
    .a(pull_resistor_25_node),
    .b({rom_3_data, LOAD_RAM, STORE_RAM, STORE_RAM_ADDR, ALU_INPUT_SWAP, SWAP_INTERNAL_FLAGS, SWAP_INTERNAL_INT, SWAP_FLAGS, SWAP_INT}),
    .eq(comparator_4_eq));  // open: gt, lt

  // Notes on the sheet:
  //   contents of rom_1 (hex, n*v repeats v):
  //   140 1 120 6 141 1 131 6 112 1 220 12 34 18 121 4 230 16 171 1 34 2 24 6 50 14 20 24 2
  //   Halt
  //   Fault
  //   Zero Fault
  //   Program ROM
  //   Program Counter
  //   Instruction register
  //   Step Counter
  //   Program Counter
  //   Normal
  //   BUS
  //   DISPLAY
  //   FAULT
  //   Microcode == 0
  //   contents of rom_2 (hex, n*v repeats v):
  //   1 78 254*0 78 255*0 78 255*0 78 3327*0 404 78 254*0 804 78 254*0 10000030 40004 78 253*0 10000030
  //   40004 78 253*0 34 78 254*0 80004004 78 254*0 80008004 78 254*0 30 4 78 2301*0 480 78 254*0 880 78
  //   254*0 10000030 40080 78 253*0 10000030 40080 78 253*0 b0 78 254*0 80004080 78 254*0 80008080 78
  //   254*0 30 80 78 2301*0 4500 78 254*0 4900 78 254*0 10000030 44100 78 253*0 10000030 44100 78 253*0
  //   4130 78 254*0 80004100 78 254*0 8000c100 78 254*0 30 4100 78 2301*0 4600 78 254*0 4a00 78 254*0
  //   10000030 44200 78 253*0 10000030 44200 78 253*0 4230 78 254*0 80004200 78 254*0 8000c200 78 254*0 30
  //   4200 78 2301*0 20000400 78 254*0 20000800 78 254*0 10000030 20040000 78 253*0 10000030 20040000 78
  //   253*0 20000030 78 254*0 a0004000 78 254*0 a0008000 78 254*0 30 20000000 78 43261*0 100400 78 254*0
  //   200400 78 254*0 400400 30 1000 78 3580*0 100800 78 254*0 200800 78 254*0 400800 30 1000 78 3580*0
  //   10000030 140000 78 253*0 10000030 240000 78 253*0 10000030 440000 30 1000 78 3579*0 10000030 140000
  //   78 253*0 10000030 240000 78 253*0 10000030 440000 30 1000 78 3579*0 100030 78 254*0 200030 78 254*0
  //   400030 30 1000 78 3580*0 80104000 78 254*0 80204000 78 254*0 80404000 30 1000 78 3580*0 80108000 78
  //   254*0 80208000 78 254*0 80408000 30 1000 78 3580*0 30 100000 78 253*0 30 200000 78 253*0 30 400000
  //   30 1000 78 36347*0 1004000 78 254*0 2004000 78 3838*0 1008000 78 254*0 2008000 78 3838*0 10000030
  //   1080000 78 253*0 10000030 2080000 78 3837*0 10000030 1080000 78 253*0 10000030 2080000 78 3837*0
  //   41000030 78 254*0 42000030 78 3838*0 41000400 78 254*0 42000400 78 3838*0 41000800 78 254*0 42000800
  //   78 16621054*0 78
  //   Microcode
  //   ALU
  //   Registers
  //   Internal Registers (for use by microcode only)
  //   Display
  //   contents of rom_3 (hex, n*v repeats v):
  //   512*0 1 255*0 2 4096*0 10 1022*0 20 80 3071*0 10 1022*0 20 80 3071*0 10 1022*0 20 80 3071*0 10
  //   1022*0 20 80 3071*0 10 1022*0 20 80 43775*0 20 40 4094*0 20 40 4095*0 20 40 3581*0 10 255*0 10 255*0
  //   10 20 40 4093*0 20 40 4094*0 20 40 4094*0 20 40 3581*0 20 80 254*0 20 80 254*0 20 80 20 40 48637*0
  //   10 255*0 10
endmodule

module ALU (
  input  [5:0] OP,
  input  [15:0] A,
  input  [15:0] B,
  input  FLAG_A,
  input  FLAG_B,
  output [15:0] OUT,
  output F_OUT
);

  wire adder_1_cout, adder_2_cout, and_2_out, comparator_1_eq, comparator_1_gt, comparator_1_lt,
       comparator_2_eq, comparator_2_gt, comparator_2_lt, decoder_1_out0, decoder_1_out1, decoder_1_out2,
       decoder_1_out3, decoder_1_out4, decoder_1_out5, decoder_1_out6, decoder_1_out7, decoder_1_out8,
       decoder_1_out9, decoder_1_out10, decoder_1_out11, decoder_1_out12, decoder_1_out13, decoder_1_out14,
       decoder_1_out15, decoder_1_out16, decoder_1_out17, decoder_1_out18, decoder_1_out19, decoder_1_out20,
       decoder_1_out21, decoder_1_out22, decoder_1_out23, decoder_1_out24, decoder_1_out25, nand_2_out,
       nor_2_out, not_2_out, not_3_out, or_2_out, pull_resistor_7_node, pull_resistor_8_node,
       pull_resistor_11_node, pull_resistor_13_node, subtractor_1_bout, subtractor_2_bout, xnor_2_out,
       xor_2_out;
  wire [1:0] pull_resistor_5_node, pull_resistor_6_node;
  wire [3:0] bitselector_1_out, bitselector_2_out;
  wire [4:0] bitadder_1_out;
  wire [15:0] adder_1_out, adder_2_out, and_1_out, bit_extender_1_out, divider_1_out, divider_1_rem,
       multiplier_1_out, nand_1_out, negator_1_out, nor_1_out, not_1_out, or_1_out, pull_resistor_9_node,
       pull_resistor_10_node, pull_resistor_12_node, pull_resistor_14_node, pull_resistor_15_node,
       shifter_1_out, shifter_2_out, subtractor_1_out, subtractor_2_out, xnor_1_out, xor_1_out;

  Pull_Resistor pull_resistor_1 (.node(FLAG_A));
  Pull_Resistor pull_resistor_2 (.node(B));
  Pull_Resistor pull_resistor_3 (.node(FLAG_B));
  Pull_Resistor pull_resistor_4 (.node(A));
  Pull_Resistor pull_resistor_5 (.node(pull_resistor_5_node));
  Pull_Resistor pull_resistor_6 (.node(pull_resistor_6_node));
  Pull_Resistor pull_resistor_7 (.node(pull_resistor_7_node));
  Pull_Resistor pull_resistor_8 (.node(pull_resistor_8_node));
  Pull_Resistor pull_resistor_9 (.node(pull_resistor_9_node));
  Pull_Resistor pull_resistor_10 (.node(pull_resistor_10_node));
  Pull_Resistor #(.pull(1)) pull_resistor_11 (.node(pull_resistor_11_node));
  Pull_Resistor pull_resistor_12 (.node(pull_resistor_12_node));
  Pull_Resistor #(.pull(1)) pull_resistor_13 (.node(pull_resistor_13_node));
  Pull_Resistor pull_resistor_14 (.node(pull_resistor_14_node));
  BitSelector #(.width(16), .group(4)) bitselector_1 (.in(B), .out(bitselector_1_out), .sel(pull_resistor_5_node));
  BitSelector #(.width(16), .group(4)) bitselector_2 (.in(B), .out(bitselector_2_out), .sel(pull_resistor_6_node));
  Pull_Resistor pull_resistor_15 (.node(pull_resistor_15_node));
  Pull_Resistor pull_resistor_16 (.node(OP));
  Adder #(.width(16)) adder_1 (.a(A), .b(B), .out(adder_1_out), .cin(pull_resistor_7_node), .cout(adder_1_cout));
  Subtractor #(.width(16)) subtractor_1 (
    .a(A), .b(B), .out(subtractor_1_out), .bin(pull_resistor_8_node), .bout(subtractor_1_bout));
  Multiplier #(.width(16)) multiplier_1 (
    .a(A), .b(B), .out(multiplier_1_out), .cin(pull_resistor_9_node));  // open: cout
  Divider #(.width(16)) divider_1 (
    .a(A), .b(B), .out(divider_1_out), .upper(pull_resistor_10_node), .rem(divider_1_rem));
  Negator #(.width(16)) negator_1 (.in(A), .out(negator_1_out));
  Adder #(.width(16)) adder_2 (
    .a(A), .b(pull_resistor_12_node), .out(adder_2_out), .cin(pull_resistor_11_node), .cout(adder_2_cout));
  Subtractor #(.width(16)) subtractor_2 (
    .a(A), .b(pull_resistor_14_node), .out(subtractor_2_out), .bin(pull_resistor_13_node),
    .bout(subtractor_2_bout));
  Shifter #(.width(16)) shifter_1 (.in(A), .\dist (bitselector_1_out), .out(shifter_1_out));
  Shifter #(.width(16), .shift("lr")) shifter_2 (.in(A), .\dist (bitselector_2_out), .out(shifter_2_out));
  BitAdder #(.width(16)) bitadder_1 (.in0(A), .out(bitadder_1_out));
  assign not_1_out = ~A;  // NOT_Gate not_1, 16 bits wide
  assign and_1_out = A & B;  // AND_Gate and_1, 16 bits wide
  assign or_1_out = A | B;  // OR_Gate or_1, 16 bits wide
  assign xor_1_out = A ^ B;  // XOR_Gate xor_1, 16 bits wide
  assign nand_1_out = ~(A & B);  // NAND_Gate nand_1, 16 bits wide
  assign nor_1_out = ~(A | B);  // NOR_Gate nor_1, 16 bits wide
  assign xnor_1_out = ~(A ^ B);  // XNOR_Gate xnor_1, 16 bits wide
  Comparator #(.width(16)) comparator_1 (
    .a(A), .b(B), .gt(comparator_1_gt), .eq(comparator_1_eq), .lt(comparator_1_lt));
  Comparator #(.width(16)) comparator_2 (
    .a(A), .b(pull_resistor_15_node), .gt(comparator_2_gt), .eq(comparator_2_eq), .lt(comparator_2_lt));
  not not_2 (not_2_out, FLAG_A);
  and and_2 (and_2_out, FLAG_A, FLAG_B);
  or or_2 (or_2_out, FLAG_A, FLAG_B);
  xor xor_2 (xor_2_out, FLAG_A, FLAG_B);
  nand nand_2 (nand_2_out, FLAG_A, FLAG_B);
  nor nor_2 (nor_2_out, FLAG_A, FLAG_B);
  xnor xnor_2 (xnor_2_out, FLAG_A, FLAG_B);
  not not_3 (not_3_out, OP[5]);
  Decoder #(.select(5)) decoder_1 (
    .out0(decoder_1_out0), .out1(decoder_1_out1), .out2(decoder_1_out2), .out3(decoder_1_out3),
    .out4(decoder_1_out4), .out5(decoder_1_out5), .out6(decoder_1_out6), .out7(decoder_1_out7),
    .out8(decoder_1_out8), .out9(decoder_1_out9), .out10(decoder_1_out10), .out11(decoder_1_out11),
    .out12(decoder_1_out12), .out13(decoder_1_out13), .out14(decoder_1_out14), .out15(decoder_1_out15),
    .out16(decoder_1_out16), .out17(decoder_1_out17), .out18(decoder_1_out18), .out19(decoder_1_out19),
    .out20(decoder_1_out20), .out21(decoder_1_out21), .out22(decoder_1_out22), .out23(decoder_1_out23),
    .out24(decoder_1_out24), .out25(decoder_1_out25), .sel(OP[4:0]), .en(not_3_out));  // open: out26, out27, out28, out29, out30, out31
  assign OUT = decoder_1_out0 ? adder_1_out : 16'bz;  // Controlled_Buffer controlled_buffer_1
  assign F_OUT = decoder_1_out0 ? adder_1_cout : 1'bz;  // Controlled_Buffer controlled_buffer_2
  assign OUT = decoder_1_out1 ? subtractor_1_out : 16'bz;  // Controlled_Buffer controlled_buffer_3
  assign F_OUT = decoder_1_out1 ? subtractor_1_bout : 1'bz;  // Controlled_Buffer controlled_buffer_4
  assign OUT = decoder_1_out2 ? multiplier_1_out : 16'bz;  // Controlled_Buffer controlled_buffer_5
  assign OUT = decoder_1_out3 ? divider_1_out : 16'bz;  // Controlled_Buffer controlled_buffer_6
  assign OUT = decoder_1_out4 ? divider_1_rem : 16'bz;  // Controlled_Buffer controlled_buffer_7
  assign OUT = decoder_1_out5 ? negator_1_out : 16'bz;  // Controlled_Buffer controlled_buffer_8
  assign OUT = decoder_1_out6 ? adder_2_out : 16'bz;  // Controlled_Buffer controlled_buffer_9
  assign F_OUT = decoder_1_out6 ? adder_2_cout : 1'bz;  // Controlled_Buffer controlled_buffer_10
  assign OUT = decoder_1_out7 ? subtractor_2_out : 16'bz;  // Controlled_Buffer controlled_buffer_11
  assign F_OUT = decoder_1_out7 ? subtractor_2_bout : 1'bz;  // Controlled_Buffer controlled_buffer_12
  assign OUT = decoder_1_out8 ? shifter_1_out : 16'bz;  // Controlled_Buffer controlled_buffer_13
  assign OUT = decoder_1_out9 ? shifter_2_out : 16'bz;  // Controlled_Buffer controlled_buffer_14
  assign OUT = decoder_1_out10 ? bit_extender_1_out : 16'bz;  // Controlled_Buffer controlled_buffer_15
  assign bit_extender_1_out = {{11{bitadder_1_out[4]}}, bitadder_1_out};  // Bit_Extender bit_extender_1
  assign OUT = decoder_1_out11 ? not_1_out : 16'bz;  // Controlled_Buffer controlled_buffer_16
  assign OUT = decoder_1_out12 ? and_1_out : 16'bz;  // Controlled_Buffer controlled_buffer_17
  assign OUT = decoder_1_out13 ? or_1_out : 16'bz;  // Controlled_Buffer controlled_buffer_18
  assign OUT = decoder_1_out14 ? xor_1_out : 16'bz;  // Controlled_Buffer controlled_buffer_19
  assign OUT = decoder_1_out15 ? nand_1_out : 16'bz;  // Controlled_Buffer controlled_buffer_20
  assign OUT = decoder_1_out16 ? nor_1_out : 16'bz;  // Controlled_Buffer controlled_buffer_21
  assign OUT = decoder_1_out17 ? xnor_1_out : 16'bz;  // Controlled_Buffer controlled_buffer_22
  assign F_OUT = decoder_1_out18 ? comparator_1_eq : 1'bz;  // Controlled_Buffer controlled_buffer_23
  assign F_OUT = decoder_1_out19 ? ~comparator_1_eq : 1'bz;  // Controlled_Inverter controlled_inverter_1
  assign F_OUT = decoder_1_out20 ? comparator_1_lt : 1'bz;  // Controlled_Buffer controlled_buffer_24
  assign F_OUT = decoder_1_out21 ? comparator_1_gt : 1'bz;  // Controlled_Buffer controlled_buffer_25
  assign F_OUT = decoder_1_out22 ? comparator_2_eq : 1'bz;  // Controlled_Buffer controlled_buffer_26
  assign F_OUT = decoder_1_out23 ? ~comparator_2_eq : 1'bz;  // Controlled_Inverter controlled_inverter_2
  assign F_OUT = decoder_1_out24 ? comparator_2_lt : 1'bz;  // Controlled_Buffer controlled_buffer_27
  assign F_OUT = decoder_1_out25 ? comparator_2_gt : 1'bz;  // Controlled_Buffer controlled_buffer_28
  assign F_OUT = decoder_1_out11 ? not_2_out : 1'bz;  // Controlled_Buffer controlled_buffer_29
  assign F_OUT = decoder_1_out12 ? and_2_out : 1'bz;  // Controlled_Buffer controlled_buffer_30
  assign F_OUT = decoder_1_out13 ? or_2_out : 1'bz;  // Controlled_Buffer controlled_buffer_31
  assign F_OUT = decoder_1_out14 ? xor_2_out : 1'bz;  // Controlled_Buffer controlled_buffer_32
  assign F_OUT = decoder_1_out15 ? nand_2_out : 1'bz;  // Controlled_Buffer controlled_buffer_33
  assign F_OUT = decoder_1_out16 ? nor_2_out : 1'bz;  // Controlled_Buffer controlled_buffer_34
  assign F_OUT = decoder_1_out17 ? xnor_2_out : 1'bz;  // Controlled_Buffer controlled_buffer_35
  Decoder #(.select(5)) decoder_2 (
    .sel(OP[4:0]), .en(OP[5]));  // open: out0, out1, out2, out3, out4, out5, out6, out7, out8, out9, out10, out11, out12, out13, out14, out15, out16, out17, out18, out19, out20, out21, out22, out23, out24, out25, out26, out27, out28, out29, out30, out31
  Pull_Resistor pull_resistor_17 (.node(F_OUT));
  Pull_Resistor pull_resistor_18 (.node(OUT));

  // Notes on the sheet:
  //   Arithmetic
  //   Bitwise logic
  //   Comparison
endmodule
