// Logisim project CPU2.circ as structural Verilog: 2 circuits, main circuit main
module main (
  output [31:0] out_1
);

  wire AluA_EnableSigned, AluA_Left_UseConst, AluA_Right_UseConst, AluA_WriteOutput, and_1_out, and_2_out,
       big_rom_1_p1, big_rom_1_p2, buffer_1_out, CLK, clock_1_out, comparator_1_eq, comparator_1_gt,
       comparator_1_lt, DoJump, DoJump_IfCompare_AluA, HALT, JumpDest_UseReg, JumpDest_UseRom,
       LoadInsn_FromRom, mini_bit_extender_2_p1, mini_bit_extender_3_p1, mini_bit_selector_4_p11,
       mini_bit_selector_4_p13, MovByte_Write, MovRam_Addr_UsePayload, MovRam_Addr_UseReg,
       MovRam_WriteFromRam, MovRam_WriteToRam, MovRegisters_A, MovRegisters_B, MovRom_Write, MovTiny_Write,
       multiplexer_1_out, not_1_out, not_2_out, not_3_out, or_2_out, or_3_out, ProgramCounter_Advance,
       pull_resistor_2_node, pull_resistor_3_node, s_r_ff_1_qn, ShouldPCJump, xor_1_out;
  wire [1:0] AluA_LeftConst_PayloadField, AluA_LeftReg_PayloadField, AluA_Op_PayloadField,
       AluA_OutReg_PayloadField, AluA_RightConst_PayloadField, AluA_RightReg_PayloadField,
       JumpCompare_AluAOp_Field, JumpDest_Reg_PayloadField, MovRam_AddrReg_PayloadField,
       MovRam_DataReg_PayloadField, MovRom_Reg_PayloadField;
  wire [2:0] JumpCompare_AluAOp;
  wire [4:0] AluA_LeftConst, AluA_LeftReg, AluA_Op, AluA_OutReg, AluA_RightConst, AluA_RightReg,
       JumpDest_Reg, MovRam_AddrReg, MovRam_DataReg, MovReg_DstA, MovReg_DstB, MovReg_SrcA, MovReg_SrcB,
       MovRom_Reg, MovTinyA_Reg, MovTinyB_Reg;
  wire [7:0] counter_2_q, pull_resistor_4_node;
  wire [11:0] IR_q;
  wire [14:0] RamAddr;
  wire [15:0] counter_1_q;
  wire [19:0] InsnPayload;
  wire [31:0] AluA_LeftReg_Value, AluA_LeftValue, AluA_Result, AluA_RightReg_Value, AluA_RightValue,
       controlled_buffer_2_out, controlled_buffer_3_out, controlled_buffer_4_out, JumpDest, MovByte_Value,
       MovTinyA_Value, MovTinyB_Value, pull_resistor_1_node, RamValue, RomValue;

  Comparator #(.width(32), .mode("unsigned")) comparator_1 (
    .a(AluA_Result), .b(pull_resistor_1_node), .gt(comparator_1_gt), .eq(comparator_1_eq),
    .lt(comparator_1_lt));
  Pull_Resistor pull_resistor_1 (.node(pull_resistor_1_node));
  not not_1 (not_1_out, comparator_1_gt);
  not not_2 (not_2_out, comparator_1_lt);
  not not_3 (not_3_out, comparator_1_eq);
  Clock clock_1 (.out(clock_1_out));
  and and_1 (and_1_out, JumpDest_UseRom, ~ShouldPCJump);  // AND_Gate
  Multiplexer #(.select(3), .enable("false")) multiplexer_1 (
    .in0(comparator_1_gt), .in1(not_1_out), .in2(comparator_1_eq), .in3(not_2_out), .in4(comparator_1_lt),
    .in5(not_3_out), .out(multiplexer_1_out), .sel(JumpCompare_AluAOp));  // open: in6, in7
  and and_2 (and_2_out, multiplexer_1_out, DoJump_IfCompare_AluA);
  xor xor_1 (xor_1_out, clock_1_out, buffer_1_out);
  buf buffer_1 (buffer_1_out, clock_1_out);
  S_R_Flip_Flop s_r_ff_1 (.S(HALT), .Qn(s_r_ff_1_qn));  // open: R, clk, Q, reset, preset
  or or_1 (ShouldPCJump, and_2_out, DoJump);
  and and_3 (CLK, xor_1_out, s_r_ff_1_qn);
  or or_2 (or_2_out, ProgramCounter_Advance, and_1_out);
  ROM #(.addrWidth(16), .dataWidth(32), .sourcepath("asm/out.hex")) PROG (.addr(counter_1_q), .data(RomValue));
  Counter #(.width(16), .max('hffff)) counter_1 (
    .load(ShouldPCJump), .up(pull_resistor_2_node), .count(or_2_out), .clk(CLK), .Q(counter_1_q));  // open: clr, D, carry
  Pull_Resistor #(.pull(1)) pull_resistor_2 (.node(pull_resistor_2_node));
  // Mini_Bit_Selector #(.in_width(32), .out_width(16)) mini_bit_selector_1: pin names not known; wires that end beside it: JumpDest
  Counter counter_2 (
    .load(LoadInsn_FromRom), .up(pull_resistor_3_node), .count(pull_resistor_3_node), .clk(CLK),
    .D(pull_resistor_4_node), .Q(counter_2_q));  // open: clr, carry
  Pull_Resistor #(.pull(1)) pull_resistor_3 (.node(pull_resistor_3_node));
  Pull_Resistor pull_resistor_4 (.node(pull_resistor_4_node));
  assign JumpDest = JumpDest_UseRom ? RomValue : 32'bz;  // Controlled_Buffer controlled_buffer_1
  Register #(.width(32)) IR (.D(RomValue), .en(LoadInsn_FromRom), .clk(CLK), .Q({IR_q, InsnPayload}));  // open: clr
  RAM #(.addrWidth(15), .dataWidth(32)) ram_1 (
    .addr(RamAddr), .we(MovRam_WriteToRam), .oe(MovRam_WriteFromRam), .clk(CLK), .data(RamValue));
  // Big_ROM #(.addressWidth(20), .valueWidth(64), .sourcepath("run/out/v2/microcode.hex")) big_rom_1: pin names not known; wires that end beside it: big_rom_1_p1, big_rom_1_p2
  // Splitter #(.fanout(32), .incoming(32), .appear("right"), .spacing("double")) splitter_1: pin names not known; wires that end beside it: big_rom_1_p1, HALT, LoadInsn_FromRom
  // Splitter #(.appear("center"), .spacing("double")) splitter_2: pin names not known; wires that end beside it: ProgramCounter_Advance, MovRom_Write, MovRom_Reg_PayloadField
  // Splitter #(.appear("center"), .spacing("double")) splitter_3: pin names not known; wires that end beside it: AluA_LeftReg_PayloadField
  // Splitter #(.appear("center"), .spacing("double")) splitter_4: pin names not known; wires that end beside it: AluA_RightReg_PayloadField
  // Splitter #(.appear("center"), .spacing("double")) splitter_5: pin names not known; wires that end beside it: AluA_OutReg_PayloadField
  // Splitter #(.appear("center"), .spacing("double")) splitter_6: pin names not known; wires that end beside it: AluA_EnableSigned, AluA_WriteOutput, DoJump, AluA_Op_PayloadField
  // Splitter #(.appear("center"), .spacing("double")) splitter_7: pin names not known; wires that end beside it: JumpDest_UseRom, JumpDest_UseReg, MovByte_Write, MovTiny_Write, JumpDest_Reg_PayloadField
  // Splitter #(.appear("center"), .spacing("double")) splitter_8: pin names not known; wires that end beside it: DoJump_IfCompare_AluA, MovRam_WriteToRam, MovRam_WriteFromRam, JumpCompare_AluAOp_Field
  // Splitter #(.appear("center"), .spacing("double")) splitter_9: pin names not known; wires that end beside it: MovRam_Addr_UsePayload, MovRam_Addr_UseReg, MovRam_DataReg_PayloadField
  // Splitter #(.fanout(32), .incoming(32), .appear("right"), .spacing("double")) splitter_10: pin names not known; wires that end beside it: big_rom_1_p2
  or or_3 (or_3_out, AluA_WriteOutput, DoJump_IfCompare_AluA);
  // Splitter #(.appear("center"), .spacing("double")) splitter_11: pin names not known; wires that end beside it: MovRam_AddrReg_PayloadField
  // Splitter #(.appear("center"), .spacing("double")) splitter_12: pin names not known; wires that end beside it: AluA_LeftConst_PayloadField
  // Splitter #(.appear("center"), .spacing("double")) splitter_13: pin names not known; wires that end beside it: AluA_Left_UseConst, AluA_Right_UseConst, MovRegisters_A, MovRegisters_B, AluA_RightConst_PayloadField
  // Probe on controlled_buffer_2_out
  // Probe on controlled_buffer_2_out
  assign controlled_buffer_2_out = or_3_out ? AluA_LeftValue : 32'bz;  // Controlled_Buffer controlled_buffer_2
  Pull_Resistor pull_resistor_5 (.node(AluA_RightValue));
  Pull_Resistor pull_resistor_6 (.node(AluA_LeftValue));
  // ALU #(.width(32)) alu_1: pin names not known; wires that end beside it: AluA_EnableSigned, AluA_Op, AluA_LeftValue, AluA_RightValue, AluA_Result
  // Probe on controlled_buffer_3_out
  // Probe on controlled_buffer_3_out
  assign controlled_buffer_3_out = or_3_out ? AluA_RightValue : 32'bz;  // Controlled_Buffer controlled_buffer_3
  // Probe on controlled_buffer_4_out
  // Probe on controlled_buffer_4_out
  assign controlled_buffer_4_out = or_3_out ? AluA_Result : 32'bz;  // Controlled_Buffer controlled_buffer_4
  Multiplexer #(.select(2), .width(5), .enable("false")) multiplexer_2 (
    .in0(InsnPayload[4:0]), .in1(InsnPayload[9:5]), .in2(InsnPayload[14:10]), .in3(InsnPayload[19:15]),
    .out(MovRom_Reg), .sel(MovRom_Reg_PayloadField));
  Multiplexer #(.select(2), .width(5), .enable("false")) multiplexer_3 (
    .in0(InsnPayload[4:0]), .in1(InsnPayload[9:5]), .in2(InsnPayload[14:10]), .in3(InsnPayload[19:15]),
    .out(AluA_LeftReg), .sel(AluA_LeftReg_PayloadField));
  Multiplexer #(.select(2), .width(5), .enable("false")) multiplexer_4 (
    .in0(InsnPayload[4:0]), .in1(InsnPayload[9:5]), .in2(InsnPayload[14:10]), .in3(InsnPayload[19:15]),
    .out(AluA_RightReg), .sel(AluA_RightReg_PayloadField));
  Multiplexer #(.select(2), .width(5), .enable("false")) multiplexer_5 (
    .in0(InsnPayload[4:0]), .in1(InsnPayload[9:5]), .in2(InsnPayload[14:10]), .in3(InsnPayload[19:15]),
    .out(AluA_OutReg), .sel(AluA_OutReg_PayloadField));
  Multiplexer #(.select(2), .width(5), .enable("false")) multiplexer_6 (
    .in0(InsnPayload[4:0]), .in1(InsnPayload[9:5]), .in2(InsnPayload[14:10]), .in3(InsnPayload[19:15]),
    .out(AluA_Op), .sel(AluA_Op_PayloadField));
  Multiplexer #(.select(2), .width(5), .enable("false")) multiplexer_7 (
    .in0(InsnPayload[4:0]), .in1(InsnPayload[9:5]), .in2(InsnPayload[14:10]), .in3(InsnPayload[19:15]),
    .out(JumpDest_Reg), .sel(JumpDest_Reg_PayloadField));
  Multiplexer #(.select(2), .width(5), .enable("false")) multiplexer_8 (
    .in0(InsnPayload[4:0]), .in1(InsnPayload[9:5]), .in2(InsnPayload[14:10]), .in3(InsnPayload[19:15]),
    .out(AluA_LeftConst), .sel(AluA_LeftConst_PayloadField));
  Multiplexer #(.select(2), .width(5), .enable("false")) multiplexer_9 (
    .in0(InsnPayload[4:0]), .in1(InsnPayload[9:5]), .in2(InsnPayload[14:10]), .in3(InsnPayload[19:15]),
    .out(AluA_RightConst), .sel(AluA_RightConst_PayloadField));
  // Mini_Bit_Extender #(.out_width(32)) mini_bit_extender_1: pin names not known; wires that end beside it: InsnPayload[7:0], MovByte_Value
  // Mini_Bit_Extender #(.in_width(5), .out_width(32)) mini_bit_extender_2: pin names not known; wires that end beside it: mini_bit_extender_2_p1, mini_bit_extender_2_p1, MovTinyB_Value
  // Mini_Bit_Extender #(.in_width(5), .out_width(32)) mini_bit_extender_3: pin names not known; wires that end beside it: mini_bit_extender_3_p1, mini_bit_extender_3_p1, MovTinyA_Value
  // Splitter #(.fanout(4), .incoming(20), .appear("center"), .spacing("double"), .bit1(0), .bit2(0), .bit3(0), .bit4(0), .bit5(1), .bit6(1), .bit7(1), .bit8(1), .bit9(1), .bit10(2), .bit11(2), .bit12(2), .bit13(2), .bit14(2), .bit15(3), .bit16(3), .bit17(3), .bit18(3), .bit19(3)) splitter_14: pin names not known; wires that end beside it: InsnPayload, MovTinyB_Reg, MovTinyA_Reg
  Controlled_Buffer #(.width(15)) controlled_buffer_5 (.out(RamAddr), .en(MovRam_Addr_UsePayload));  // open: in
  // Mini_Bit_Selector #(.in_width(20), .out_width(15)) mini_bit_selector_2: pin names not known; wires that end beside it: InsnPayload
  Multiplexer #(.select(2), .width(5), .enable("false")) multiplexer_10 (
    .in0(InsnPayload[4:0]), .in1(InsnPayload[9:5]), .in2(InsnPayload[14:10]), .in3(InsnPayload[19:15]),
    .out(MovRam_AddrReg), .sel(MovRam_AddrReg_PayloadField));
  Multiplexer #(.select(2), .width(5), .enable("false")) multiplexer_11 (
    .in0(InsnPayload[4:0]), .in1(InsnPayload[9:5]), .in2(InsnPayload[14:10]), .in3(InsnPayload[19:15]),
    .out(MovRam_DataReg), .sel(MovRam_DataReg_PayloadField));
  Multiplexer #(.select(2), .width(5), .enable("false")) multiplexer_12 (
    .in0(InsnPayload[4:0]), .in1(InsnPayload[9:5]), .in2(InsnPayload[14:10]), .in3(InsnPayload[19:15]),
    .sel(JumpCompare_AluAOp_Field));  // open: out
  // Splitter #(.fanout(4), .incoming(20), .appear("center"), .spacing("double"), .bit1(0), .bit2(0), .bit3(0), .bit4(0), .bit5(1), .bit6(1), .bit7(1), .bit8(1), .bit9(1), .bit10(2), .bit11(2), .bit12(2), .bit13(2), .bit14(2), .bit15(3), .bit16(3), .bit17(3), .bit18(3), .bit19(3)) splitter_15: pin names not known; wires that end beside it: InsnPayload, MovReg_DstB, MovReg_SrcB, MovReg_DstA, MovReg_SrcA
  // Mini_Bit_Selector #(.in_width(5), .out_width(3)) mini_bit_selector_3: pin names not known; wires that end beside it: JumpCompare_AluAOp
  Multiplexer #(.width(32), .enable("false")) multiplexer_13 (
    .in0(AluA_LeftReg_Value), .out(AluA_LeftValue), .sel(AluA_Left_UseConst));  // open: in1
  // Mini_Bit_Extender #(.in_width(5), .out_width(32)) mini_bit_extender_4: pin names not known; wires that end beside it: AluA_LeftConst
  Multiplexer #(.width(32), .enable("false")) multiplexer_14 (
    .in0(AluA_RightReg_Value), .out(AluA_RightValue), .sel(AluA_Right_UseConst));  // open: in1
  // Mini_Bit_Extender #(.in_width(5), .out_width(32)) mini_bit_extender_5: pin names not known; wires that end beside it: AluA_RightConst
  // Register_Bank #(.width(32), .registerCount(32), .portCount(32)) register_bank_1: pin names not known; wires that end beside it: JumpDest_Reg, AluA_OutReg, AluA_RightReg, AluA_LeftReg, MovRom_Reg, CLK, MovByte_Value, AluA_WriteOutput, AluA_Result, MovRom_Write, RomValue, out_1, AluA_RightReg_Value, AluA_LeftReg_Value
  // Mini_Bit_Selector #(.in_width(32), .out_width(15)) mini_bit_selector_4: pin names not known; wires that end beside it: MovReg_DstB, MovReg_SrcB, MovReg_DstA, MovReg_SrcA, MovRam_AddrReg, MovRam_DataReg, MovTinyB_Reg, MovTinyA_Reg, InsnPayload[19:15], MovRegisters_B, mini_bit_selector_4_p11, MovRegisters_A, mini_bit_selector_4_p13, MovRam_WriteFromRam, RamValue, MovTiny_Write, MovTinyB_Value, MovTiny_Write, MovTinyA_Value, mini_bit_selector_4_p11, mini_bit_selector_4_p13, MovRam_Addr_UseReg, MovRam_WriteToRam, RamValue, JumpDest_UseReg, JumpDest, RamAddr

  // Other names for the same wires on the sheet: MovByte_Reg[4:0] = InsnPayload[19:15]

  // Notes on the sheet:
  //   contents of PROG (hex, n*v repeats v):
  //   408840 e08800 308001 310000 b00441 b30424 1018800 8b0c85 e 820462 3 b00822 700000 6 b01425 e09400
  //   b00400 700000 3
  //   ±
  //   +
  //   =
endmodule

module viewer (
);

  wire [31:0] main_1_out_1;

  main main_1 (.out_1(main_1_out_1));
  // Probe on main_1_out_1
endmodule
